# Fritzing sketch circuit (saved by Fritzing 0.9.3b)

parts:
  SparkFun_ESP8266_Thing1 = SparkFun ESP8266 Thing
  IR_Sensor = Adafruit AMG8833 8x8 GRID EYE
  LiPo_Battery = Battery Holders [package=lipo-1100mAh]
  R1 = Resistor [tolerance=±5% resistance=27k package=THT]
  R2 = Resistor [tolerance=±5% resistance=100k package=THT]
  Status_LED = LED - 5mm [color="Blue (430nm)" package="5 mm [THT]"]
  Wake-Up_Button = Round Pushbutton

nets:
  GND: SparkFun_ESP8266_Thing1.GND, IR_Sensor.GND, LiPo_Battery.-, R1.Pin_1, Status_LED.cathode, Wake-Up_Button.leg1
  N1: SparkFun_ESP8266_Thing1.VBAT, LiPo_Battery.+, R2.Pin_1
  N2: SparkFun_ESP8266_Thing1.GPIO4, Status_LED.anode
  N3: SparkFun_ESP8266_Thing1.ADC, R1.Pin_0, R2.Pin_0
  N4: SparkFun_ESP8266_Thing1.DTR, Wake-Up_Button.leg0
  VCC: SparkFun_ESP8266_Thing1.VCC, IR_Sensor.VIN
  N5: SparkFun_ESP8266_Thing1.GPIO2/SDA, IR_Sensor.SDA
  N6: SparkFun_ESP8266_Thing1.GPIO14/SCL, IR_Sensor.SCL

custom parts:
  SparkFun ESP8266 Thing: The SparkFun ESP8266 Thing is a breakout and development board for the ESP8266 WiFi SoC – a leading platform for Internet of Things (IoT) or WiFi-related projects. The Thing is low-cost and easy to use, and Arduino IDE integration can be achieved in just a few steps. We’ve made the ESP8266 easy to use by breaking out all of the module’s pins, adding a LiPo charger, power supply, and all of the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
